// Logisim project logic_gates.circ as structural Verilog: 7 circuits, main circuit and_gate
module and_gate (
  input  A,
  input  B,
  output Y
);

  and and_1 (Y, A, B);

  // Notes on the sheet:
  //   AND GATE
endmodule

module or_gate (
  input  A,
  input  B,
  output Y
);

  or or_1 (Y, A, B);

  // Notes on the sheet:
  //   OR GATE
endmodule

module xor_gate (
  input  A,
  input  B,
  output Y
);

  xor xor_1 (Y, A, B);

  // Notes on the sheet:
  //   XOR GATE
endmodule

module inverter_gate (
  input  A,
  output Y
);

  not not_1 (Y, A);

  // Notes on the sheet:
  //   INVERTER GATE
endmodule

module nand_gate (
  input  A,
  input  B,
  output Y
);

  nand nand_1 (Y, A, B);

  // Notes on the sheet:
  //   NAND GATE
endmodule

module nor_gate (
  input  A,
  input  B,
  output Y
);

  nor nor_1 (Y, A, B);

  // Notes on the sheet:
  //   NOR GATE
endmodule

module xnor_gate (
  input  A,
  input  B,
  output Y
);

  xnor xnor_1 (Y, A, B);

  // Notes on the sheet:
  //   XNOR GATE
endmodule
