// Logisim project adders.circ as structural Verilog: 4 circuits, main circuit half_adder
module half_adder (
  input  A,
  input  B,
  output Sum,
  output Cout
);

  xor xor_1 (Sum, A, B);
  and and_1 (Cout, A, B);

  // Notes on the sheet:
  //   Author: Emmanuel Adoum
  //   Title: CE Student
  //   Country: Chad
  //   Date: 27th, August 2026
  //   HALF ADDER
endmodule

module full_adder (
  input  A,
  input  B,
  input  Cin,
  output Sum,
  output Cout
);

  wire and_1_out, and_2_out, xor_1_out;

  xor xor_1 (xor_1_out, A, B);
  and and_1 (and_1_out, xor_1_out, Cin);
  and and_2 (and_2_out, B, A);
  xor xor_2 (Sum, xor_1_out, Cin);
  or or_1 (Cout, and_1_out, and_2_out);

  // Notes on the sheet:
  //   Author: Emmanuel Adoum
  //   Title: CE Student
  //   Country: Chad
  //   Date: 27th, August 2026
  //   FULL ADDER
endmodule

module ripple_carry_adder_4bit (
  input  [3:0] A,
  input  [3:0] B,
  output [3:0] Sum,
  output Cout
);

  wire full_adder_1_cout, full_adder_2_cout, full_adder_3_cout;

  full_adder full_adder_1 (.A(A[0]), .B(B[0]), .Cin(1'b0), .Sum(Sum[0]), .Cout(full_adder_1_cout));
  full_adder full_adder_2 (.A(A[1]), .B(B[1]), .Cin(full_adder_1_cout), .Sum(Sum[1]), .Cout(full_adder_2_cout));
  full_adder full_adder_3 (.A(A[2]), .B(B[2]), .Cin(full_adder_2_cout), .Sum(Sum[2]), .Cout(full_adder_3_cout));
  full_adder full_adder_4 (.A(A[3]), .B(B[3]), .Cin(full_adder_3_cout), .Sum(Sum[3]), .Cout(Cout));

  // Notes on the sheet:
  //   Author: Emmanuel Adoum
  //   Title: CE Student
  //   Country: Chad
  //   Date: 27th, August 2026
  //   RIPPLE CARRY ADDER 4 BIT
endmodule

module ripple_carry_adder_8bit (
  input  [7:0] A,
  input  [7:0] B,
  output [7:0] Sum,
  output Cout
);

  wire full_adder_1_cout, full_adder_2_cout, full_adder_3_cout, full_adder_4_cout, full_adder_5_cout,
       full_adder_6_cout, full_adder_7_cout;

  full_adder full_adder_1 (.A(A[0]), .B(B[0]), .Cin(1'b0), .Sum(Sum[0]), .Cout(full_adder_1_cout));
  full_adder full_adder_2 (.A(A[1]), .B(B[1]), .Cin(full_adder_1_cout), .Sum(Sum[1]), .Cout(full_adder_2_cout));
  full_adder full_adder_3 (.A(A[2]), .B(B[2]), .Cin(full_adder_2_cout), .Sum(Sum[2]), .Cout(full_adder_3_cout));
  full_adder full_adder_4 (.A(A[3]), .B(B[3]), .Cin(full_adder_3_cout), .Sum(Sum[3]), .Cout(full_adder_4_cout));
  full_adder full_adder_5 (.A(A[4]), .B(B[4]), .Cin(full_adder_4_cout), .Sum(Sum[4]), .Cout(full_adder_5_cout));
  full_adder full_adder_6 (.A(A[5]), .B(B[5]), .Cin(full_adder_5_cout), .Sum(Sum[5]), .Cout(full_adder_6_cout));
  full_adder full_adder_7 (.A(A[6]), .B(B[6]), .Cin(full_adder_6_cout), .Sum(Sum[6]), .Cout(full_adder_7_cout));
  full_adder full_adder_8 (.A(A[7]), .B(B[7]), .Cin(full_adder_7_cout), .Sum(Sum[7]), .Cout(Cout));

  // Notes on the sheet:
  //   Author: Emmanuel Adoum
  //   Title: CE Student
  //   Country: Chad
  //   Date: 27th, August 2026
  //   RIPPLE CARRY ADDER 8 BIT
endmodule
